# Fritzing sketch Quadcopter Wiring (saved by Fritzing 0.9.3b)

parts:
  Raspberry_Pi_1 = Raspberry Pi 3 [part_number=RPI-3-V1.2]
  GY1 = GY-5150 (MPU-9150) [form="♀ (female)" package=THT]
  Part1 = ESC MLF1218
  920KV_Motor1 = DJI 920 KV Motor
  Part2 = ESC MLF1218
  Part3 = ESC MLF1218
  Part4 = ESC MLF1218
  920KV_Motor2 = DJI 920 KV Motor
  920KV_Motor3 = DJI 920 KV Motor
  920KV_Motor4 = DJI 920 KV Motor
  U1 = mystery part, 3 pins [chip_label=?]
  U2 = mystery part, 3 pins [chip_label=?]
  U3 = mystery part, 3 pins [chip_label=?]
  U4 = mystery part, 3 pins [chip_label=?]
  Ground = female pin header, 2 pins [form="♀ (female)"]  # not connected
  U5 = LIPO-110mAh [package=lipo-110]  # not connected

nets:
  N1: Raspberry_Pi_1.3v3, GY1.pin1
  N2: Raspberry_Pi_1.GPIO2, GY1.pin3
  N3: Raspberry_Pi_1.GPIO3, GY1.pin4
  N4: Raspberry_Pi_1.GPIO5, U1.pin1
  N5: Raspberry_Pi_1.GPIO6, U2.pin1
  N6: Raspberry_Pi_1.GPIO13, U3.pin1
  N7: Raspberry_Pi_1.GPIO26, U4.pin1
  N8: Part1.GND*, 920KV_Motor2.w
  N9: Part1.PPM, 920KV_Motor1.v, Part4.+5, 920KV_Motor2.v
  N10: Part1.+5, 920KV_Motor2.u
  N11: 920KV_Motor1.w, Part4.GND*
  N12: 920KV_Motor1.u, Part4.PPM
  N13: Part2.GND*, 920KV_Motor3.w
  N14: Part2.PPM, 920KV_Motor3.v
  N15: Part2.+5, 920KV_Motor3.u
  N16: Part3.GND*, 920KV_Motor4.w
  N17: Part3.PPM, 920KV_Motor4.u
  N18: Part3.+5, 920KV_Motor4.v

notes:
  The red wire from the ESC boards can be used to power the RPi, but can lead to melting board components.
  These green wires connect to the GPIO pins to provide a PWM output to the ESCs.
  These are the ESCs. The type we will be using combines the functionality of 4 separate ESCs into one board.
  These are brushless DC motors. They require a cyclical AC signal which is provided by the ESC. Swapping the order of the wires changes the direction of rotation.
  This is a sample gyroscope and accelerometer board. The RPi reads values from the sensors using I2C peripherals.
  This is a LiPo battery that will be used to power the RPi and the ESCs.

custom parts:
  GY-5150 (MPU-9150): Placa GY-5150 basada en conjunto de acelerómetro+giroscopios+magnetómetro MPU-9150
  ESC MLF1218: ESC (Electronic Speed Control) for Cheerson CX-20 quadcopter
  DJI 920 KV Motor: DJI Brushless Outrunner 2212/920K Motor F330-550
